# Fritzing sketch circuit_design (saved by Fritzing 1.0.2b)
breadboards: 2

parts:
  J1 = Screw terminal - 2 pins [package=THT]
  Arduino_Nano = Arduino Nano (Rev3.0)
  J3 = Screw terminal - 2 pins [package=THT]
  J2 = screw terminal, 2 pins
  J4 = Screw terminal - 2 pins [package=THT]
  J5 = Screw terminal - 2 pins [package=THT]
  J6 = Screw terminal - 2 pins [package=THT]
  Stepper_B = Stepper Motor - Bipolar
  Stepper_A = Stepper Motor - Bipolar
  Stepper_C = Stepper Motor - Bipolar
  TMC2208-A = TMC2209 [package=THT]
  TMC2208-B = TMC2209 [package=THT]
  TMC2208-C = TMC2209 [package=THT]
  part = Electrolytic Capacitor [capacitance=100µF voltage=35V package="1010 [SMD, electrolytic]"]
  part_2 = Electrolytic Capacitor [capacitance=100µF voltage=35V package="1010 [SMD, electrolytic]"]
  part_3 = Electrolytic Capacitor [capacitance=100µF voltage=35V package="1010 [SMD, electrolytic]"]
  12V_1A = Hanmatek HM305
  Resistive_Touch_Screen = Generic male header - 4 pins [form="♂ (male)" package=THT]

nets:
  N1: J1.pin1, Stepper_A.D, TMC2208-A.M2B
  N2: J1.pin2, Stepper_A.B, TMC2208-A.M2A
  GND: Arduino_Nano.GND, TMC2208-A.GND, TMC2208-B.GND, TMC2208-C.GND, part.-, part_2.-, part_3.-, 12V_1A.Pin_3
  N3: Arduino_Nano.D2, TMC2208-A.EN, TMC2208-B.EN, TMC2208-C.EN
  N4: Arduino_Nano.D3, TMC2208-A.Step
  N5: Arduino_Nano.D4, TMC2208-A.Dir
  N6: Arduino_Nano.D5, TMC2208-B.Step
  N7: Arduino_Nano.D6, TMC2208-B.Dir
  N8: Arduino_Nano.D7, TMC2208-C.Step
  N9: Arduino_Nano.D8, TMC2208-C.Dir
  N10: Arduino_Nano.5V, TMC2208-A.VIO, TMC2208-A.MS1, TMC2208-A.MS2, TMC2208-B.VIO, TMC2208-B.MS1, TMC2208-B.MS2, TMC2208-C.VIO, TMC2208-C.MS1, TMC2208-C.MS2
  N11: Arduino_Nano.A3, Resistive_Touch_Screen.X-
  N12: Arduino_Nano.A2, Resistive_Touch_Screen.Y-
  N13: Arduino_Nano.A1, Resistive_Touch_Screen.X+
  N14: Arduino_Nano.A0, Resistive_Touch_Screen.Y+
  N15: J3.pin1, Stepper_C.D, TMC2208-C.M2B
  N16: J3.pin2, Stepper_C.B, TMC2208-C.M2A
  N17: J2.pin1, Stepper_B.D, TMC2208-B.M2B
  N18: J2.pin2, Stepper_B.B, TMC2208-B.M2A
  N19: J4.pin1, Stepper_A.A, TMC2208-A.M1B
  N20: J4.pin2, Stepper_A.C, TMC2208-A.M1A
  N21: J5.pin1, Stepper_B.A, TMC2208-B.M1B
  N22: J5.pin2, Stepper_B.C, TMC2208-B.M1A
  N23: J6.pin1, Stepper_C.A, TMC2208-C.M1B
  N24: J6.pin2, Stepper_C.C, TMC2208-C.M1A
  N25: TMC2208-A.VM, TMC2208-B.VM, TMC2208-C.VM, part.+, part_2.+, part_3.+, 12V_1A.Pin_4

notes:
  12.00
  1.000

custom parts:
  TMC2209: TMC2209-LA stepper motor controller and driver. Supply voltage 4.75-28V Iphase up to 1.77A rms (2.5A peak)
  Hanmatek HM305: DC Power Supply 30V5A HM305.
  Generic male header - 4 pins: Generic male header
